// Digital circuit ClockSelect.dig as structural Verilog
module ClockSelect (
  input  DIV0,
  input  DIV1,
  input  CLK,
  input  RES,
  output DIV_CLK
);

  wire CLK_4, CLK_8, CLK_16;

  _74HC393 _74hc393_1 (.CLK(CLK), .CLR(RES), .Q_B(CLK_4), .Q_C(CLK_8), .Q_D(CLK_16));  // open: Q_A
  _74153 _74153_1 (
    .pin1(1'b0), .pin2(DIV1), .pin3(CLK_16), .pin4(CLK_8), .pin5(CLK_4), .pin6(CLK), .pin7(DIV_CLK),
    .pin8(1'b0), .pin10(1'b0), .pin11(1'b0), .pin12(1'b0), .pin13(1'b0), .pin14(DIV0), .pin15(1'b1),
    .pin16(1'b1));  // open: pin9

  // Notes on the sheet:
  //   RES: Active-high reset line, pin 1
endmodule

/* Test case 1/4 clock:
CLK RES  DIV0 DIV1	DIV_CLK
0   1    1    0		0
C   0    1    0		0
C   0    1    0		1
C   0    1    0		1
C   0    1    0		0
C   0    1    0		0
C   0    1    0		1
C   0    1    0		1
C   1    1    0		0
C   0    1    0		0
C   0    1    0		1
C   0    1    0		1
C   0    1    0		0
C   0    1    0		0
C   0    1    0		1
C   0    1    0		1
*/

/* Test case 1/8 clock:
CLK RES  DIV0 DIV1	DIV_CLK
0   1    0    1		0
C   0    0    1		0
C   0    0    1		0
C   0    0    1		0
C   0    0    1		1
C   0    0    1		1
C   0    0    1		1
C   0    0    1		1
C   1    0    1		0
C   0    0    1		0
C   0    0    1		0
C   0    0    1		0
C   0    0    1		1
C   0    0    1		1
C   0    0    1		1
C   0    0    1		1
*/

/* Test case 1/16 clock:
CLK RES  DIV0 DIV1	DIV_CLK
0   1    1    1		0
C   0    1    1		0
C   0    1    1		0
C   0    1    1		0
C   0    1    1		0
C   0    1    1		0
C   0    1    1		0
C   0    1    1		0
C   0    1    1		1
C   0    1    1		1
C   0    1    1		1
C   0    1    1		1
C   0    1    1		1
C   0    1    1		1
C   0    1    1		1
C   0    1    1		1
*/
