// Digital circuit StateMachine.dig as structural Verilog
module StateMachine (
  input  nRES,
  input  CLK,
  input  RUNNING,
  output TXC,
  output SPI_CLK
);

  wire nand_1_out;

  nand nand_1 (nand_1_out, nRES, RUNNING);
  _74HC393 _74hc393_1 ();
  _74HC393 _74hc393_2 ();

  // Notes on the sheet:
  //   TXC: pin 5
  //   nRES: pin 2, default 1
  //   CLK: pin 1
  //   RUNNING: pin 4
  //   SPI_CLK: pin 7
endmodule

/* Test case:
CLK ~RES TXC
0   1    0
C   1    0
C   1    0
C   1    0
C   1    0
C   1    0
C   1    0
C   1    0
C   1    1
*/
